# Fritzing sketch Ultrasonic Car Schematic (saved by Fritzing 0.9.3b)
breadboards: 1

parts:
  Raspberry_Pi_Zero1 = Raspberry Pi Zero
  MD03A1 = Dual VNH2SP30 Motor Driver [part_number=MD03A]
  BAT2 = Battery Holders [package=battery-aa-kit]
  BAT1 = Battery Holders [package=battery-aa]
  BAT3 = Battery Holders [package=battery-aa]
  M1 = DC Motor
  M2 = DC Motor
  R1 = Resistor [tolerance=±5% resistance=1k package="2512 [SMD]"]
  R2 = Resistor [tolerance=±5% resistance=1k package="2512 [SMD]"]
  LED1 = LED - 5mm [color="Red (633nm)" package="5 mm [THT]"]
  LED2 = LED - 5mm [color="Red (633nm)" package="5 mm [THT]"]
  hc-sr1 = hc-sr04
  R3 = Resistor [tolerance=±5% resistance=1k package="2512 [SMD]"]
  R4 = Resistor [tolerance=±5% resistance=2k package="2512 [SMD]"]

nets:
  N1: Raspberry_Pi_Zero1.GPIO27, hc-sr1.Trig
  N2: Raspberry_Pi_Zero1.GPIO22, R3.Pin_0, R4.Pin_0
  N3: Raspberry_Pi_Zero1.GPIO21, LED2.anode
  N4: Raspberry_Pi_Zero1.GPIO20, LED1.anode
  N5: Raspberry_Pi_Zero1.GPIO8, MD03A1.2INb#143
  N6: Raspberry_Pi_Zero1.GPIO25, MD03A1.2INb#142
  N7: Raspberry_Pi_Zero1.GPIO15, MD03A1.1INb
  N8: Raspberry_Pi_Zero1.GPIO14, MD03A1.1INa
  GND: Raspberry_Pi_Zero1.GND, R1.Pin_0, R2.Pin_0, hc-sr1.GND, R4.Pin_1
  5V: Raspberry_Pi_Zero1.5V, hc-sr1.VCC
  N9: MD03A1.GND, BAT1.+
  N10: MD03A1.+5V_(IN), BAT3.-
  N11: MD03A1.OUT_1A, M2.pin_1
  N12: MD03A1.OUT_1B, M2.pin_2
  N13: MD03A1.OUT_2A, M1.pin_1
  N14: MD03A1.OUT_2B, M1.pin_2
  N15: BAT2.+, BAT1.-
  N16: BAT2.-, BAT3.+
  N17: R1.Pin_1, LED1.cathode
  N18: R2.Pin_1, LED2.cathode
  N19: hc-sr1.Echo, R3.Pin_1

notes:
  Steering Motor
  Driving Motor
